# Fritzing sketch Esquema B (saved by Fritzing 1.0.1rc)
breadboards: 1

parts:
  Controlador_de_servos1 = 16-Channel 12-bit PWM Servo Driver - I2C [part_number=815]
  Raspberri_Pi_4B2 = Raspberry Pi 4B
  OLED2 = SSD1306 0.96in 128x64 I2C Monochrome OLED Display
  OLED3 = SSD1306 0.96in 128x64 I2C Monochrome OLED Display
  BN-880_GPS1 = u-blox NEO-6M GPS Breakout
  BN-880_GPS_(Compass)1 = Compass Module - HMC6352
  RASPBERRY_PI_V2_CAMERA2 = Rasberry Pi NIOR Camera [chip_label=IC package="DIP (Dual Inline) [THT]"]  # not connected
  Ultrasons_1 = HC-SR04 Ultrasonic Distance Sensor
  MPU-6050_Acceleròmetre_i_Giroscopi1 = InvenSense MPU6050
  Componente2 = Adafruit MAX98357A I2S 3W Class D Amplifier [part_number="Adafruit #3006"]
  ALTAVOZ_CON_CAJA_-_3W1 = SPEAKER [package=pcb_mount_speaker]
  Servo_5 = Basic Servo
  Servo_6 = Basic Servo
  Servo_7 = Basic Servo
  Servo_8 = Basic Servo
  Servo_9 = Basic Servo
  Servo_10 = Basic Servo
  Servo_11 = Basic Servo
  Servo_12 = Basic Servo
  Servo_13 = Basic Servo
  VR1 = LM2574 (DIP) [part_number=LM2574 package="DIP (Dual Inline) [THT]"]
  VCC3 = Battery
  VCC4 = Battery
  VR2 = LM2574 (DIP) [part_number=LM2574 package="DIP (Dual Inline) [THT]"]

nets:
  N1: Controlador_de_servos1.PWRIN, VR1.pin2
  GND: Controlador_de_servos1.GND, Servo_5.gnd, Servo_6.gnd, Servo_7.gnd, Servo_8.gnd, Servo_9.gnd, Servo_10.gnd, Servo_11.gnd, Servo_12.gnd, Servo_13.gnd, VR1.pin4
  N2: Controlador_de_servos1.PWM5, Servo_8.pulse
  VCC: Controlador_de_servos1.5.0V, Servo_5.vcc, Servo_6.vcc, Servo_7.vcc, Servo_8.vcc, Servo_9.vcc, Servo_10.vcc, Servo_11.vcc, Servo_12.vcc, Servo_13.vcc
  N3: Controlador_de_servos1.PWM4, Servo_7.pulse
  N4: Controlador_de_servos1.PWM1, Servo_6.pulse
  N5: Controlador_de_servos1.PWM0, Servo_5.pulse
  VCC_2: Controlador_de_servos1.VCC, Raspberri_Pi_4B2.3V3, Raspberri_Pi_4B2.GPIO24, OLED2.VCC, OLED3.VCC, MPU-6050_Acceleròmetre_i_Giroscopi1.VCC
  5V: Controlador_de_servos1.SDA, Raspberri_Pi_4B2.5V, Raspberri_Pi_4B2.GPIO2, BN-880_GPS1.Pin_1, Ultrasons_1.VCC
  N6: Controlador_de_servos1.SCL, Controlador_de_servos1.OE, Raspberri_Pi_4B2.GPIO3
  N7: Controlador_de_servos1.PWM15, Servo_13.pulse
  N8: Controlador_de_servos1.PWM13, Servo_12.pulse
  N9: Controlador_de_servos1.PWM12, Servo_9.pulse
  N10: Controlador_de_servos1.PWM9, Servo_11.pulse
  N11: Controlador_de_servos1.PWM8, Servo_10.pulse
  GND_2: Raspberri_Pi_4B2.GND, Raspberri_Pi_4B2.GPIO27, Raspberri_Pi_4B2.GPIO10, Raspberri_Pi_4B2.GPIO5, OLED2.GND, OLED2.SDA, OLED3.GND, OLED3.SCL, BN-880_GPS1.Pin_2, BN-880_GPS_(Compass)1.SDA, Ultrasons_1.GND, MPU-6050_Acceleròmetre_i_Giroscopi1.GND, Componente2.GND
  N12: Raspberri_Pi_4B2.GPIO4, OLED2.SCL
  N13: Raspberri_Pi_4B2.GPIO14, BN-880_GPS1.Pin_3
  N14: Raspberri_Pi_4B2.GPIO15, BN-880_GPS1.Pin_4
  N15: Raspberri_Pi_4B2.GPIO17, Raspberri_Pi_4B2.GPIO18, OLED3.SDA, Componente2.BCLK
  N16: Raspberri_Pi_4B2.GPIO23, Ultrasons_1.ECHO
  N17: Raspberri_Pi_4B2.GPIO9, Raspberri_Pi_4B2.GPIO25, BN-880_GPS_(Compass)1.SCL
  N18: Raspberri_Pi_4B2.GPIO8, Ultrasons_1.TRIG
  N19: Raspberri_Pi_4B2.GPIO6, MPU-6050_Acceleròmetre_i_Giroscopi1.SDA
  N20: Raspberri_Pi_4B2.GPIO13, MPU-6050_Acceleròmetre_i_Giroscopi1.SCL
  N21: Raspberri_Pi_4B2.GPIO19, Componente2.LRCLK
  N22: Raspberri_Pi_4B2.GPIO21, Componente2.DIN
  N23: Componente2.VO-, ALTAVOZ_CON_CAJA_-_3W1.+
  N24: Componente2.VO+, ALTAVOZ_CON_CAJA_-_3W1.-
  N25: VR1.pin3, VCC3.-
  N26: VR1.pin5, VCC3.+
  N27: VCC4.-, VR2.pin3
  N28: VCC4.+, VR2.pin5

notes:
  GPS BN-880
  SDA
  SCL
  Camera OV5647
  SERVOMOTORS MG996R Digital Servomotor
  Audio Amplificator
  RASPBERRY PI 4 MODEL B
  for Raspberry Pi
  PCA 9685
  Ultrasonic Distance Sensor HC-SR04
  OLED Screen Module
  GY-521 MODULE (MPU-6050 accelerometer and gyro)
  Micròfon connectat per USB a la Raspberry
  (16 channel
  SSD1306 GME12864-11-12-13
  (0.96in, 128x64)
  (Dual GPS/GLONASS with integrated compass)
  I2S MAX98357 (3W)
  Speaker
  PWM controller)
  Raspberry alimentada a través de port USB-C amb 5V estables obtinguts de una de les LIPOs (Lipo d'abaix) un cop passat pel conversor de voltatge.
  DC-DC 5V 3A - S13V30F5 Voltage Conversor
  3500mAh 2S 25C LiPo Battery (7.4V)
  Voltatge resultant es transmet a la Raspberry Pi 4B a través de USB-C

custom parts:
  16-Channel 12-bit PWM Servo Driver - I2C: You want to make a cool robot, maybe a hexapod walker, or maybe just a piece of art with a lot of moving parts. Or maybe you want to drive a lot of LEDs with precise PWM output. Using only two pins, control 16 free-running PWM outputs! You can even chain up 62 breakouts to control up to 992 PWM outputs.
  Rasberry Pi NIOR Camera: Camera
  Adafruit MAX98357A I2S 3W Class D Amplifier: Listen to this good news - we now have an all in one digital audio amp breakout board that works incredibly well with the Raspberry Pi! If you're looking for an easy and low cost way to get you digital sound files bumpin' then the MAX08357 I2S Amp Breakout is for you. It takes standard I2S digital audio input and, not only decodes it into analog, but also amplifies it directly into a speaker.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
  Battery: Your standard 2x AA battery pack (3 Volts)
